# Fritzing sketch Technologische kant (saved by Fritzing 0.8.7b)
breadboards: 1

parts:
  Luidspreker_is_verbonden_aan_de_aux_van_de_RPI = Raspberry Pi 4B
  S1 = Pushbutton [package=THT]
  R1 = Resistor [tolerance=±5% resistance=10k package=THT]
  R2 = Resistor [tolerance=±5% resistance=10k package=THT]
  R3 = Resistor [tolerance=±5% resistance=10k package=THT]
  S2 = Pushbutton [package=THT]
  S3 = Pushbutton [package=THT]
  S4 = Pushbutton [package=THT]
  R4 = Resistor [tolerance=±5% resistance=10k package=THT]
  S5 = Pushbutton [package=THT]
  R5 = Resistor [tolerance=±5% resistance=10k package=THT]
  S6 = Pushbutton [package=THT]
  R6 = Resistor [tolerance=±5% resistance=10k package=THT]
  S7 = Pushbutton [package=THT]
  R7 = Resistor [tolerance=±5% resistance=10k package=THT]
  S8 = Pushbutton [package=THT]
  R8 = Resistor [tolerance=±5% resistance=10k package=THT]
  S9 = Pushbutton [package=THT]
  R9 = Resistor [tolerance=±5% resistance=10k package=THT]
  S10 = Pushbutton [package=THT]
  R10 = Resistor [tolerance=±5% resistance=10k package=THT]
  S11 = Pushbutton [package=THT]
  R11 = Resistor [tolerance=±5% resistance=10k package=THT]
  S12 = Pushbutton [package=THT]
  R12 = Resistor [tolerance=±5% resistance=10k package=THT]
  S13 = Pushbutton [package=THT]
  S14 = Pushbutton [package=THT]
  S15 = Pushbutton [package=THT]
  S16 = Pushbutton [package=THT]
  S17 = Pushbutton [package=THT]
  S18 = Pushbutton [package=THT]
  S19 = Pushbutton [package=THT]
  S20 = Pushbutton [package=THT]
  S21 = Pushbutton [package=THT]
  S22 = Pushbutton [package=THT]
  S23 = Pushbutton [package=THT]
  S24 = Pushbutton [package=THT]
  R13 = Resistor [tolerance=±5% resistance=10k package=THT]
  R14 = Resistor [tolerance=±5% resistance=10k package=THT]
  R15 = Resistor [tolerance=±5% resistance=10k package=THT]
  R16 = Resistor [tolerance=±5% resistance=10k package=THT]
  R17 = Resistor [tolerance=±5% resistance=10k package=THT]
  R18 = Resistor [tolerance=±5% resistance=10k package=THT]
  R19 = Resistor [tolerance=±5% resistance=10k package=THT]
  R20 = Resistor [tolerance=±5% resistance=10k package=THT]
  R21 = Resistor [tolerance=±5% resistance=10k package=THT]
  R22 = Resistor [tolerance=±5% resistance=10k package=THT]
  R23 = Resistor [tolerance=±5% resistance=10k package=THT]
  R24 = Resistor [tolerance=±5% resistance=10k package=THT]
  SP1 = SPEAKER [package=pcb_mount_speaker]

nets:
  N1: Luidspreker_is_verbonden_aan_de_aux_van_de_RPI.3V3, R2.Pin_1, R3.Pin_1, R4.Pin_1, R5.Pin_1, R6.Pin_1, R7.Pin_1, R8.Pin_1, R9.Pin_1, R10.Pin_1, R11.Pin_1, R12.Pin_1, R13.Pin_1, R14.Pin_1, R15.Pin_1, R16.Pin_1, R17.Pin_1, R18.Pin_1, R19.Pin_1, R20.Pin_1, R21.Pin_1, R22.Pin_1, R23.Pin_1, R24.Pin_1
  N2: Luidspreker_is_verbonden_aan_de_aux_van_de_RPI.GPIO2, S13.leg1, R17.Pin_0
  N3: Luidspreker_is_verbonden_aan_de_aux_van_de_RPI.GPIO3, S16.leg1, R24.Pin_0
  N4: Luidspreker_is_verbonden_aan_de_aux_van_de_RPI.GPIO4, S22.leg1, R19.Pin_0
  N5: Luidspreker_is_verbonden_aan_de_aux_van_de_RPI.GPIO14, S12.leg1, R12.Pin_0
  N6: Luidspreker_is_verbonden_aan_de_aux_van_de_RPI.GPIO15, S11.leg1, R11.Pin_0
  N7: Luidspreker_is_verbonden_aan_de_aux_van_de_RPI.GPIO17, S21.leg1, R23.Pin_0
  N8: Luidspreker_is_verbonden_aan_de_aux_van_de_RPI.GPIO18, S10.leg1, R10.Pin_0
  N9: Luidspreker_is_verbonden_aan_de_aux_van_de_RPI.GPIO27, S18.leg1, R13.Pin_0
  N10: Luidspreker_is_verbonden_aan_de_aux_van_de_RPI.GPIO22, S20.leg1, R15.Pin_0
  N11: Luidspreker_is_verbonden_aan_de_aux_van_de_RPI.GPIO23, S9.leg1, R9.Pin_0
  N12: Luidspreker_is_verbonden_aan_de_aux_van_de_RPI.GPIO24, S8.leg1, R8.Pin_0
  N13: Luidspreker_is_verbonden_aan_de_aux_van_de_RPI.GPIO10, S19.leg1, R20.Pin_0
  N14: Luidspreker_is_verbonden_aan_de_aux_van_de_RPI.GPIO9, S24.leg1, R14.Pin_0
  N15: Luidspreker_is_verbonden_aan_de_aux_van_de_RPI.GPIO25, S7.leg1, R7.Pin_0
  N16: Luidspreker_is_verbonden_aan_de_aux_van_de_RPI.GPIO11, S17.leg1, R21.Pin_0
  N17: Luidspreker_is_verbonden_aan_de_aux_van_de_RPI.GPIO8, S6.leg1, R6.Pin_0
  N18: Luidspreker_is_verbonden_aan_de_aux_van_de_RPI.GPIO7, S5.leg1, R5.Pin_0
  N19: Luidspreker_is_verbonden_aan_de_aux_van_de_RPI.GPIO5, S23.leg1, R22.Pin_0
  N20: Luidspreker_is_verbonden_aan_de_aux_van_de_RPI.GPIO6, S14.leg1, R16.Pin_0
  N21: Luidspreker_is_verbonden_aan_de_aux_van_de_RPI.GPIO12, S4.leg1, R4.Pin_0
  N22: Luidspreker_is_verbonden_aan_de_aux_van_de_RPI.GPIO13, S15.leg1, R18.Pin_0
  N23: Luidspreker_is_verbonden_aan_de_aux_van_de_RPI.GND, S1.leg0, S2.leg0, S3.leg0, S4.leg0, S5.leg0, S6.leg0, S7.leg0, S8.leg0, S9.leg0, S10.leg0, S11.leg0, S12.leg0, S13.leg0, S14.leg0, S15.leg0, S16.leg0, S17.leg0, S18.leg0, S20.leg0, S21.leg0, S22.leg0, S23.leg0, S24.leg0
  N24: Luidspreker_is_verbonden_aan_de_aux_van_de_RPI.GPIO16, R3.Pin_0, S3.leg1
  N25: Luidspreker_is_verbonden_aan_de_aux_van_de_RPI.GPIO20, R2.Pin_0, S2.leg1
  N26: Luidspreker_is_verbonden_aan_de_aux_van_de_RPI.GPIO21, S1.leg1, R1.Pin_0
  N27: Luidspreker_is_verbonden_aan_de_aux_van_de_RPI.RUN, SP1.+
